# Fritzing sketch Op-Amp_Mic_1 (saved by Fritzing 0.9.3b)
breadboards: 1

parts:
  U1 = LM 358 Dual Op-Amp [package="DIP8 [THT]"]
  Cmod_A1 = Cmod A7
  A1 = Dual Output Sensor Module (VMA309)

nets:
  N1: U1.connector0, Cmod_A1.A15
  N2: U1.connector2, A1.A0
  GND: U1.connector3, Cmod_A1.GND, A1.GND
  N3: U1.connector7, Cmod_A1.VU, A1.V+
  N4: Cmod_A1.1, A1.D0

custom parts:
  Cmod A7: The Digilent Cmod A7 is a small, 48-pin DIP form factor board built around a Xilinx Artix 7 FPGA. The board also includes a USB-JTAG programming circuit, USB-UART bridge, clock source, Pmod host connector, SRAM, Quad SPI Flash, and basic I/O devices. These components make it a formidable, albeit compact, platform for digital logic circuits and Microblaze embedded softcore processor designs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
